// Logisim project BC.circ as structural Verilog: 25 circuits, main circuit main
module main (
  input  [7:0] INPR,
  output [2:0] out_2,
  output [15:0] out_3,
  output [15:0] out_4
);

  wire ac_ctrl_1_clr, ac_ctrl_1_inc, ac_ctrl_1_ld, alu_1_e_2, ar_ctrl_1_clr, ar_ctrl_1_inr, ar_ctrl_1_ld,
       CLK, clock_1_out, dr_ctrl_1_inr, dr_ctrl_1_ld, E, e_ctrl_1_clr, e_ctrl_1_cmp, e_ctrl_1_ld, FGI, FGO,
       HLT, IEN, ir_ctrl_1_ld, j_k_ff_1_q, memory_ctrl_1_ld, not_1_out, or_1_out, outr_ctrl_1_ld,
       pc_ctrl_1_clr, pc_ctrl_1_inr, pc_ctrl_1_ld, R, t_ctrl_1_out_4, tr_ctrl_1_ld;
  wire [2:0] alu_ctrl_1_out_3;
  wire [3:0] T;
  wire [7:0] OUPUT;
  wire [11:0] AR, PC;
  wire [15:0] alu_1_out_6, bus_1_out_9, controlled_buffer_1_out, controlled_buffer_2_out, IR, tr_1_out_6;

  ALU alu_1 (.AC(out_4), .DR(out_3), .INPR(INPR), .E(E), .out_6(alu_1_out_6), .in_4(alu_ctrl_1_out_3), .E_2(alu_1_e_2));
  E e_1 (.in_2(alu_1_e_2), .out_6(E), .CLK(CLK), .LD(e_ctrl_1_ld), .CLR(e_ctrl_1_clr), .COM(e_ctrl_1_cmp));
  E___CTRL e_ctrl_1 (.CLR(e_ctrl_1_clr), .CMP(e_ctrl_1_cmp), .LD(e_ctrl_1_ld), .T(T), .IR(IR));
  ALU___CTRL alu_ctrl_1 (.out_3(alu_ctrl_1_out_3), .T(T), .IR(IR));
  AR ar_1 (.in_1(bus_1_out_9), .INR(ar_ctrl_1_inr), .LD(ar_ctrl_1_ld), .CLK(CLK), .CLR(ar_ctrl_1_clr), .out_6(AR));
  AR___CTRl ar_ctrl_1 (.LD(ar_ctrl_1_ld), .INR(ar_ctrl_1_inr), .CLR(ar_ctrl_1_clr), .IR(IR), .T(T), .R(R));
  PC___CTRL pc_ctrl_1 (
    .R(R), .INR(pc_ctrl_1_inr), .LD(pc_ctrl_1_ld), .CLR(pc_ctrl_1_clr), .T(T), .DR(out_3), .FGI(FGI),
    .FGO(FGO), .E(E), .AC(out_4), .IR(IR));
  DR___CTRL dr_ctrl_1 (.LD(dr_ctrl_1_ld), .INR(dr_ctrl_1_inr), .IR(IR), .T(T));
  AC ac_1 (.in_1(alu_1_out_6), .INR(ac_ctrl_1_inc), .LD(ac_ctrl_1_ld), .CLK(CLK), .CLR(ac_ctrl_1_clr), .out_6(out_4));
  AC___CTRL ac_ctrl_1 (.LD(ac_ctrl_1_ld), .INC(ac_ctrl_1_inc), .CLR(ac_ctrl_1_clr), .T(T), .IR(IR));
  IR___CTRL ir_ctrl_1 (.R(R), .LD(ir_ctrl_1_ld), .T(T));
  TR___CTRL tr_ctrl_1 (.R(R), .LD(tr_ctrl_1_ld), .T(T));
  OUTR___CTRL outr_ctrl_1 (.LD(outr_ctrl_1_ld), .T(T), .IR(IR));
  Memory___CTRL memory_ctrl_1 (.R(R), .LD(memory_ctrl_1_ld), .IR(IR), .T(T));
  PC pc_1 (.in_1(bus_1_out_9), .INR(pc_ctrl_1_inr), .CLK(CLK), .CLR(pc_ctrl_1_clr), .LD(pc_ctrl_1_ld), .out_6(PC));
  DR dr_1 (.in_1(bus_1_out_9), .INR(dr_ctrl_1_inr), .LD(dr_ctrl_1_ld), .CLK(CLK), .out_6(out_3));  // open: CLR
  IR ir_1 (.LD(ir_ctrl_1_ld), .CLK(CLK), .in_1(bus_1_out_9), .out_4(IR), .HLT(HLT));
  TR tr_1 (.in_1(bus_1_out_9), .LD(tr_ctrl_1_ld), .CLK(CLK), .out_6(tr_1_out_6));  // open: INR, CLR
  OUTR outr_1 (.LD(outr_ctrl_1_ld), .CLK(CLK), .out_4(OUPUT), .in_1(bus_1_out_9));
  assign controlled_buffer_1_out = not_1_out ? bus_1_out_9 : 16'bz;  // Controlled_Buffer controlled_buffer_1
  RAM #(.addrWidth(12), .dataWidth(16)) ram_1 (
    .addr(AR), .data(controlled_buffer_1_out), .clk(CLK), .ld(memory_ctrl_1_ld));  // open: sel, clr
  assign controlled_buffer_2_out = memory_ctrl_1_ld ? controlled_buffer_1_out : 16'bz;  // Controlled_Buffer controlled_buffer_2
  not not_1 (not_1_out, memory_ctrl_1_ld);
  BUS___CTRL bus_ctrl_1 (.R(R), .out_4(out_2), .T(T), .IR(IR));
  BUS bus_1 (
    .in_8(out_2), .M(controlled_buffer_2_out), .AR(AR), .DR(out_3), .AC(out_4), .IR(IR), .TR(tr_1_out_6),
    .out_9(bus_1_out_9), .PC(PC));
  Hex_Digit_Display hex_digit_display_1 (.value(OUPUT[3:0]));  // open: dp
  Hex_Digit_Display hex_digit_display_2 (.value(OUPUT[7:4]));  // open: dp
  Clock clock_1 (.out(clock_1_out));
  T t_1 (.out_3(T), .CLR(or_1_out), .CLK(CLK));
  or or_1 (or_1_out, t_ctrl_1_out_4, HLT);
  T___CTRL t_ctrl_1 (.R(R), .out_4(t_ctrl_1_out_4), .T(T), .IR(IR));
  Hex_Digit_Display hex_digit_display_3 (.value(AR[7:4]));  // open: dp
  Hex_Digit_Display hex_digit_display_4 (.value(T));  // open: dp
  and and_1 (CLK, clock_1_out, j_k_ff_1_q);
  J_K_Flip_Flop j_k_ff_1 (.J(1'b0), .clk(clock_1_out), .K(HLT), .Q(j_k_ff_1_q));  // open: Qn, preset, en, reset
  IEN_FGI_FGO_R_FF ien_fgi_fgo_r_ff_1 (.INPR(INPR), .FGI(FGI), .FGO(FGO), .IEN(IEN), .R(R), .IR(IR), .T(T), .CLK(CLK));
  Hex_Digit_Display hex_digit_display_5 (.value(AR[3:0]));  // open: dp
  Hex_Digit_Display hex_digit_display_6 (.value(PC[7:4]));  // open: dp
  Hex_Digit_Display hex_digit_display_7 (.value(PC[3:0]));  // open: dp

  // Other names for the same wires on the sheet: AC[15:0] = out_4; DR[15:0] = out_3; INP[7:0] = INPR
endmodule

module AR (
  input  [15:0] in_1,
  input  INR,
  input  LD,
  input  CLK,
  input  CLR,
  output [11:0] out_6
);

  wire or_1_out;
  wire [11:0] multiplexer_1_out, Sum;

  Multiplexer #(.width(12)) multiplexer_1 (
    .in0(in_1[11:0]), .in1(Sum), .out(multiplexer_1_out), .sel(INR));  // open: en
  or or_1 (or_1_out, INR, LD);
  Shift_Register #(.length(12)) shift_register_1 (
    .shift(1'b0), .clk(CLK), .load(or_1_out), .clr(CLR), .d0(multiplexer_1_out[11]), .q0(out_6[11]),
    .d1(multiplexer_1_out[10]), .q1(out_6[10]), .d2(multiplexer_1_out[9]), .q2(out_6[9]),
    .d3(multiplexer_1_out[8]), .q3(out_6[8]), .d4(multiplexer_1_out[7]), .q4(out_6[7]),
    .d5(multiplexer_1_out[6]), .q5(out_6[6]), .d6(multiplexer_1_out[5]), .q6(out_6[5]),
    .d7(multiplexer_1_out[4]), .q7(out_6[4]), .d8(multiplexer_1_out[3]), .q8(out_6[3]),
    .d9(multiplexer_1_out[2]), .q9(out_6[2]), .d10(multiplexer_1_out[1]), .q10(out_6[1]),
    .d11(multiplexer_1_out[0]), .q11(out_6[0]));  // open: in, out
  Adder #(.width(12)) adder_1 (.a(out_6), .b(12'h1), .out(Sum), .cin(1'b0));  // open: cout
endmodule

module PC (
  input  [15:0] in_1,
  input  INR,
  input  LD,
  input  CLK,
  input  CLR,
  output [11:0] out_6
);

  wire or_1_out;
  wire [11:0] multiplexer_1_out, Sum;

  Multiplexer #(.width(12)) multiplexer_1 (
    .in0(in_1[11:0]), .in1(Sum), .out(multiplexer_1_out), .sel(INR));  // open: en
  or or_1 (or_1_out, INR, LD);
  Shift_Register #(.length(12)) shift_register_1 (
    .shift(1'b0), .clk(CLK), .load(or_1_out), .clr(CLR), .d0(multiplexer_1_out[11]), .q0(out_6[11]),
    .d1(multiplexer_1_out[10]), .q1(out_6[10]), .d2(multiplexer_1_out[9]), .q2(out_6[9]),
    .d3(multiplexer_1_out[8]), .q3(out_6[8]), .d4(multiplexer_1_out[7]), .q4(out_6[7]),
    .d5(multiplexer_1_out[6]), .q5(out_6[6]), .d6(multiplexer_1_out[5]), .q6(out_6[5]),
    .d7(multiplexer_1_out[4]), .q7(out_6[4]), .d8(multiplexer_1_out[3]), .q8(out_6[3]),
    .d9(multiplexer_1_out[2]), .q9(out_6[2]), .d10(multiplexer_1_out[1]), .q10(out_6[1]),
    .d11(multiplexer_1_out[0]), .q11(out_6[0]));  // open: in, out
  Adder #(.width(12)) adder_1 (.a(out_6), .b(12'h1), .out(Sum), .cin(1'b0));  // open: cout
endmodule

module TR (
  input  [15:0] in_1,
  input  INR,
  input  LD,
  input  CLK,
  input  CLR,
  output [15:0] out_6
);

  wire or_1_out;
  wire [15:0] multiplexer_1_out, Sum;

  Multiplexer #(.width(16)) multiplexer_1 (.in0(in_1), .in1(Sum), .out(multiplexer_1_out), .sel(INR));  // open: en
  or or_1 (or_1_out, INR, LD);
  Shift_Register #(.length(16)) shift_register_1 (
    .shift(1'b0), .clk(CLK), .load(or_1_out), .clr(CLR), .d0(multiplexer_1_out[15]), .q0(out_6[15]),
    .d1(multiplexer_1_out[14]), .q1(out_6[14]), .d2(multiplexer_1_out[13]), .q2(out_6[13]),
    .d3(multiplexer_1_out[12]), .q3(out_6[12]), .d4(multiplexer_1_out[11]), .q4(out_6[11]),
    .d5(multiplexer_1_out[10]), .q5(out_6[10]), .d6(multiplexer_1_out[9]), .q6(out_6[9]),
    .d7(multiplexer_1_out[8]), .q7(out_6[8]), .d8(multiplexer_1_out[7]), .q8(out_6[7]),
    .d9(multiplexer_1_out[6]), .q9(out_6[6]), .d10(multiplexer_1_out[5]), .q10(out_6[5]),
    .d11(multiplexer_1_out[4]), .q11(out_6[4]), .d12(multiplexer_1_out[3]), .q12(out_6[3]),
    .d13(multiplexer_1_out[2]), .q13(out_6[2]), .d14(multiplexer_1_out[1]), .q14(out_6[1]),
    .d15(multiplexer_1_out[0]), .q15(out_6[0]));  // open: in, out
  Adder #(.width(16)) adder_1 (.a(out_6), .b(16'h1), .out(Sum), .cin(1'b0));  // open: cout
endmodule

module DR (
  input  [15:0] in_1,
  input  INR,
  input  LD,
  input  CLK,
  input  CLR,
  output [15:0] out_6
);

  wire or_1_out;
  wire [15:0] multiplexer_1_out, Sum;

  Multiplexer #(.width(16)) multiplexer_1 (.in0(in_1), .in1(Sum), .out(multiplexer_1_out), .sel(INR));  // open: en
  or or_1 (or_1_out, INR, LD);
  Shift_Register #(.length(16)) shift_register_1 (
    .shift(1'b0), .clk(CLK), .load(or_1_out), .clr(CLR), .d0(multiplexer_1_out[15]), .q0(out_6[15]),
    .d1(multiplexer_1_out[14]), .q1(out_6[14]), .d2(multiplexer_1_out[13]), .q2(out_6[13]),
    .d3(multiplexer_1_out[12]), .q3(out_6[12]), .d4(multiplexer_1_out[11]), .q4(out_6[11]),
    .d5(multiplexer_1_out[10]), .q5(out_6[10]), .d6(multiplexer_1_out[9]), .q6(out_6[9]),
    .d7(multiplexer_1_out[8]), .q7(out_6[8]), .d8(multiplexer_1_out[7]), .q8(out_6[7]),
    .d9(multiplexer_1_out[6]), .q9(out_6[6]), .d10(multiplexer_1_out[5]), .q10(out_6[5]),
    .d11(multiplexer_1_out[4]), .q11(out_6[4]), .d12(multiplexer_1_out[3]), .q12(out_6[3]),
    .d13(multiplexer_1_out[2]), .q13(out_6[2]), .d14(multiplexer_1_out[1]), .q14(out_6[1]),
    .d15(multiplexer_1_out[0]), .q15(out_6[0]));  // open: in, out
  Adder #(.width(16)) adder_1 (.a(out_6), .b(16'h1), .out(Sum), .cin(1'b0));  // open: cout
endmodule

module IR (
  input  [15:0] in_1,
  input  LD,
  input  CLK,
  output [15:0] out_4,
  output HLT
);

  Shift_Register #(.length(16)) shift_register_1 (
    .shift(1'b0), .clk(CLK), .load(LD), .d0(in_1[15]), .q0(out_4[15]), .d1(in_1[14]), .q1(out_4[14]),
    .d2(in_1[13]), .q2(out_4[13]), .d3(in_1[12]), .q3(out_4[12]), .d4(in_1[11]), .q4(out_4[11]),
    .d5(in_1[10]), .q5(out_4[10]), .d6(in_1[9]), .q6(out_4[9]), .d7(in_1[8]), .q7(out_4[8]), .d8(in_1[7]),
    .q8(out_4[7]), .d9(in_1[6]), .q9(out_4[6]), .d10(in_1[5]), .q10(out_4[5]), .d11(in_1[4]), .q11(out_4[4]),
    .d12(in_1[3]), .q12(out_4[3]), .d13(in_1[2]), .q13(out_4[2]), .d14(in_1[1]), .q14(out_4[1]),
    .d15(in_1[0]), .q15(out_4[0]));  // open: in, out, clr
  and and_1 (HLT, out_4[0], ~out_4[1], ~out_4[2], ~out_4[3], ~out_4[4], ~out_4[5], ~out_4[6], ~out_4[7], ~out_4[8], ~out_4[9], ~out_4[10], ~out_4[11], out_4[12], out_4[13], out_4[14], ~out_4[15]);  // AND_Gate
endmodule

module AC (
  input  [15:0] in_1,
  input  INR,
  input  LD,
  input  CLK,
  input  CLR,
  output [15:0] out_6
);

  wire or_1_out;
  wire [15:0] multiplexer_1_out, Sum;

  Multiplexer #(.width(16)) multiplexer_1 (.in0(in_1), .in1(Sum), .out(multiplexer_1_out), .sel(INR));  // open: en
  or or_1 (or_1_out, INR, LD);
  Shift_Register #(.length(16)) shift_register_1 (
    .shift(1'b0), .clk(CLK), .load(or_1_out), .clr(CLR), .d0(multiplexer_1_out[15]), .q0(out_6[15]),
    .d1(multiplexer_1_out[14]), .q1(out_6[14]), .d2(multiplexer_1_out[13]), .q2(out_6[13]),
    .d3(multiplexer_1_out[12]), .q3(out_6[12]), .d4(multiplexer_1_out[11]), .q4(out_6[11]),
    .d5(multiplexer_1_out[10]), .q5(out_6[10]), .d6(multiplexer_1_out[9]), .q6(out_6[9]),
    .d7(multiplexer_1_out[8]), .q7(out_6[8]), .d8(multiplexer_1_out[7]), .q8(out_6[7]),
    .d9(multiplexer_1_out[6]), .q9(out_6[6]), .d10(multiplexer_1_out[5]), .q10(out_6[5]),
    .d11(multiplexer_1_out[4]), .q11(out_6[4]), .d12(multiplexer_1_out[3]), .q12(out_6[3]),
    .d13(multiplexer_1_out[2]), .q13(out_6[2]), .d14(multiplexer_1_out[1]), .q14(out_6[1]),
    .d15(multiplexer_1_out[0]), .q15(out_6[0]));  // open: in, out
  Adder #(.width(16)) adder_1 (.a(out_6), .b(16'h1), .out(Sum), .cin(1'b0));  // open: cout
endmodule

module ALU (
  input  [15:0] AC,
  input  [15:0] DR,
  input  [7:0] INPR,
  input  [2:0] in_4,
  input  E,
  output [15:0] out_6,
  output E_2
);

  wire AdderCO;
  wire [0:0] shifter_1_out;
  wire [14:0] SFTR;
  wire [15:0] adder_1_out, and_1_out, not_1_out;
  wire [15:1] SFTL;
  wire [15:15] shifter_2_out;

  Shifter #(.width(16)) shifter_1 (.in(AC), .\dist (4'b0001), .out({SFTL, shifter_1_out[0]}));
  Shifter #(.width(16), .shift("lr")) shifter_2 (.in(AC), .\dist (4'b0001), .out({shifter_2_out[15], SFTR}));
  Adder #(.width(16)) adder_1 (.a(AC), .b(DR), .out(adder_1_out), .cin(1'b0), .cout(AdderCO));
  assign and_1_out = DR & AC;  // AND_Gate and_1, 16 bits wide
  assign not_1_out = ~AC;  // NOT_Gate not_1, 16 bits wide
  Multiplexer #(.select(3), .width(16)) multiplexer_1 (
    .in0(AC), .in1(and_1_out), .in2(adder_1_out), .in3(not_1_out), .in4(DR), .in5({{8{1'b0}}, INPR}),
    .in6({E, SFTR}), .in7({SFTL, E}), .out(out_6), .sel(in_4));  // open: en
  Multiplexer #(.select(3)) multiplexer_2 (
    .in2(AdderCO), .in6(AC[0]), .in7(AC[15]), .out(E_2), .sel(in_4));  // open: in0, in1, in3, in4, in5, en

  // Other names for the same wires on the sheet: INPR_t[7:0] = INPR; SFTL[0] = E; SFTR[15] = E
endmodule

module OUTR (
  input  [15:0] in_1,
  input  LD,
  input  CLK,
  output [7:0] out_4
);

  Shift_Register shift_register_1 (
    .shift(1'b0), .clk(CLK), .load(LD), .d0(in_1[7]), .q0(out_4[7]), .d1(in_1[6]), .q1(out_4[6]),
    .d2(in_1[5]), .q2(out_4[5]), .d3(in_1[4]), .q3(out_4[4]), .d4(in_1[3]), .q4(out_4[3]), .d5(in_1[2]),
    .q5(out_4[2]), .d6(in_1[1]), .q6(out_4[1]), .d7(in_1[0]), .q7(out_4[0]));  // open: in, out, clr
endmodule

module T (
  input  CLK,
  input  CLR,
  output [3:0] out_3
);

  wire and_1_out, or_1_out;

  Counter #(.width(4), .max('hf)) counter_1 (
    .count(1'b1), .Q(out_3), .clk(CLK), .clr(or_1_out));  // open: load, D, carry
  and and_1 (and_1_out, out_3[0], out_3[1], out_3[2]);
  or or_1 (or_1_out, and_1_out, CLR);
endmodule

module E (
  input  CLK,
  input  in_2,
  input  LD,
  input  CLR,
  input  COM,
  output out_6
);

  wire controlled_buffer_1_out, d_ff_1_q, d_ff_1_qn, not_1_out, not_2_out;

  not not_1 (not_1_out, LD);
  assign controlled_buffer_1_out = not_1_out ? d_ff_1_q : 1'bz;  // Controlled_Buffer controlled_buffer_1
  assign controlled_buffer_1_out = LD ? in_2 : 1'bz;  // Controlled_Buffer controlled_buffer_2
  not not_2 (not_2_out, COM);
  D_Flip_Flop d_ff_1 (
    .clk(CLK), .D(controlled_buffer_1_out), .Q(d_ff_1_q), .Qn(d_ff_1_qn), .reset(CLR));  // open: preset, en
  assign out_6 = not_2_out ? d_ff_1_q : 1'bz;  // Controlled_Buffer controlled_buffer_3
  assign out_6 = COM ? d_ff_1_qn : 1'bz;  // Controlled_Buffer controlled_buffer_4
endmodule

module IEN_FGI_FGO_R_FF (
  input  [7:0] INPR,
  input  [15:0] IR,
  input  [3:0] T,
  input  CLK,
  output FGI,
  output FGO,
  output IEN,
  output R
);

  wire and_3_out, and_4_out, and_5_out, and_6_out, and_7_out, and_8_out, and_9_out, D0, D1, D2, D3, D4, D5,
       D6, D7, or_1_out, or_2_out, or_3_out, p, r_t, T0, T1, T2, T3, T4, T5, T6, T7, T8, T9, T10, T11, T12,
       T13, T14, T15;

  Decoder #(.select(3)) decoder_1 (
    .out0(D0), .out1(D1), .out2(D2), .out3(D3), .out4(D4), .out5(D5), .out6(D6), .out7(D7), .sel(IR[14:12]));  // open: en
  Decoder #(.select(4)) decoder_2 (
    .out0(T0), .out1(T1), .out2(T2), .out3(T3), .out4(T4), .out5(T5), .out6(T6), .out7(T7), .out8(T8),
    .out9(T9), .out10(T10), .out11(T11), .out12(T12), .out13(T13), .out14(T14), .out15(T15), .sel(T));  // open: en
  and and_1 (r_t, D7, ~IR[15], T3);  // AND_Gate
  and and_2 (p, D7, IR[15], T3);
  or or_1 (or_1_out, FGO, FGI);
  or or_2 (or_2_out, INPR[0], INPR[1], INPR[2], INPR[3], INPR[4], INPR[5], INPR[6], INPR[7]);
  and and_3 (and_3_out, p, IR[11]);
  and and_4 (and_4_out, p, IR[10]);
  and and_5 (and_5_out, p, IR[7]);
  and and_6 (and_6_out, p, IR[6]);
  or or_3 (or_3_out, and_6_out, and_7_out);
  and and_7 (and_7_out, R, T2);
  and and_8 (and_8_out, IEN, or_1_out, ~T0, ~T1, ~T2);  // AND_Gate
  and and_9 (and_9_out, T2, R);
  J_K_Flip_Flop j_k_ff_1 (.J(or_2_out), .clk(CLK), .K(and_3_out), .Q(FGI));  // open: Qn, preset, en, reset
  J_K_Flip_Flop j_k_ff_2 (.J(T0), .clk(CLK), .K(and_4_out), .Q(FGO));  // open: Qn, preset, en, reset
  J_K_Flip_Flop j_k_ff_3 (.J(and_5_out), .clk(CLK), .K(or_3_out), .Q(IEN));  // open: Qn, preset, en, reset
  J_K_Flip_Flop j_k_ff_4 (.J(and_8_out), .K(and_9_out), .Q(R));  // open: clk, Qn, preset, en, reset

  // Other names for the same wires on the sheet: B0 = IR[0]; B1 = IR[1]; B2 = IR[2]; B3 = IR[3]; B4 = IR[4];
  //   B5 = IR[5]; B6 = IR[6]; B7 = IR[7]; B8 = IR[8]; B9 = IR[9]; B10 = IR[10]; B11 = IR[11]; I = IR[15]
endmodule

module BUS___CTRL (
  input  [15:0] IR,
  input  [3:0] T,
  input  R,
  output [2:0] out_4
);

  wire and_2_out, and_3_out, and_4_out, and_5_out, and_6_out, and_7_out, and_8_out, and_9_out, and_10_out,
       and_11_out, and_12_out, and_13_out, and_14_out, and_17_out, and_18_out, D0, D1, D2, D3, D4, D5, D6,
       D7, p, T0, T1, T2, T3, T4, T5, T6, T7, T8, T9, T10, T11, T12, T13, T14, T15, X1, X2, X3, X4, X5, X6,
       X7;

  Decoder #(.select(3)) decoder_1 (
    .out0(D0), .out1(D1), .out2(D2), .out3(D3), .out4(D4), .out5(D5), .out6(D6), .out7(D7), .sel(IR[14:12]));  // open: en
  Decoder #(.select(4)) decoder_2 (
    .out0(T0), .out1(T1), .out2(T2), .out3(T3), .out4(T4), .out5(T5), .out6(T6), .out7(T7), .out8(T8),
    .out9(T9), .out10(T10), .out11(T11), .out12(T12), .out13(T13), .out14(T14), .out15(T15), .sel(T));  // open: en
  and and_1 (p, D7, IR[15], T3);
  and and_2 (and_2_out, D4, T4);
  or or_1 (X1, and_2_out, and_3_out);
  and and_3 (and_3_out, D5, T5);
  and and_4 (and_4_out, D3, T4);
  or or_2 (X4, and_4_out, and_5_out);
  and and_5 (and_5_out, p, IR[10]);
  and and_6 (and_6_out, ~R, T1);  // AND_Gate
  and and_7 (and_7_out, T4, D0);
  and and_8 (and_8_out, D1, T4);
  and and_9 (and_9_out, D2, T4);
  and and_10 (and_10_out, D6, T4);
  and and_11 (and_11_out, IR[15], ~D7, T3);  // AND_Gate
  or or_3 (X7, and_6_out, and_7_out, and_8_out, and_9_out, and_10_out, and_11_out);
  and and_12 (and_12_out, R, T0);
  and and_13 (and_13_out, ~R, T0);  // AND_Gate
  and and_14 (and_14_out, D5, T4);
  and and_15 (X5, ~R, T2);  // AND_Gate
  and and_16 (X6, R, T1);
  or or_4 (X2, and_12_out, and_13_out, and_14_out);
  Priority_Encoder priority_encoder_1 (
    .in1(X7), .in2(X1), .in3(X2), .in4(X3), .in5(X4), .in6(X5), .in7(X6), .out(out_4));  // open: in0, en_in, gs, en_out
  and and_17 (and_17_out, D2, T5);
  and and_18 (and_18_out, D6, T6);
  or or_5 (X3, and_17_out, and_18_out);

  // Other names for the same wires on the sheet: B0 = IR[0]; B1 = IR[1]; B2 = IR[2]; B3 = IR[3]; B4 = IR[4];
  //   B5 = IR[5]; B6 = IR[6]; B7 = IR[7]; B8 = IR[8]; B9 = IR[9]; B10 = IR[10]; B11 = IR[11]; I = IR[15]
endmodule

module PC___CTRL (
  input  [15:0] DR,
  input  [15:0] IR,
  input  [3:0] T,
  input  FGI,
  input  E,
  input  FGO,
  input  [15:0] AC,
  input  R,
  output LD,
  output CLR,
  output INR
);

  wire AC_star, and_1_out, and_2_out, and_3_out, and_4_out, and_5_out, and_6_out, and_7_out, and_8_out,
       and_9_out, and_10_out, and_11_out, and_12_out, and_13_out, D0, D1, D2, D3, D4, D5, D6, D7, DR_t, T0,
       T1, T2, T3, T4, T5, T6, T7, T8, T9, T10, T11, T12, T13, T14, T15;

  Decoder #(.select(4)) decoder_1 (
    .out0(T0), .out1(T1), .out2(T2), .out3(T3), .out4(T4), .out5(T5), .out6(T6), .out7(T7), .out8(T8),
    .out9(T9), .out10(T10), .out11(T11), .out12(T12), .out13(T13), .out14(T14), .out15(T15), .sel(T));  // open: en
  Decoder #(.select(3)) decoder_2 (
    .out0(D0), .out1(D1), .out2(D2), .out3(D3), .out4(D4), .out5(D5), .out6(D6), .out7(D7), .sel(IR[14:12]));  // open: en
  or or_1 (DR_t, DR[0], DR[1], DR[2], DR[3], DR[4], DR[5], DR[6], DR[7], DR[8], DR[9], DR[10], DR[11], DR[12], DR[13], DR[14], DR[15]);
  or or_2 (AC_star, AC[0], AC[1], AC[2], AC[3], AC[4], AC[5], AC[6], AC[7], AC[8], AC[9], AC[10], AC[11], AC[12], AC[13], AC[14], AC[15]);
  and and_1 (and_1_out, D7, ~IR[15], T3);  // AND_Gate
  and and_2 (and_2_out, D7, IR[15], T3);
  and and_3 (and_3_out, ~R, T1);  // AND_Gate
  and and_4 (and_4_out, R, T2);
  and and_5 (and_5_out, D6, T6, ~DR_t);  // AND_Gate
  and and_6 (and_6_out, ~AC[15], IR[4], and_1_out);  // AND_Gate
  and and_7 (and_7_out, AC[15], IR[3], and_1_out);
  and and_8 (and_8_out, ~AC_star, IR[2], and_1_out);  // AND_Gate
  and and_9 (and_9_out, ~E, IR[1], and_1_out);  // AND_Gate
  and and_10 (and_10_out, IR[9], FGI, and_2_out);
  and and_11 (and_11_out, FGO, IR[8], and_2_out);
  and and_12 (and_12_out, D4, T4);
  and and_13 (and_13_out, D5, T5);
  and and_14 (CLR, R, T1);
  or or_3 (INR, and_3_out, and_4_out, and_5_out, and_6_out, and_7_out, and_8_out, and_9_out, and_10_out, and_11_out);
  or or_4 (LD, and_12_out, and_13_out);

  // Other names for the same wires on the sheet: B0 = IR[0]; B1 = IR[1]; B2 = IR[2]; B3 = IR[3]; B4 = IR[4];
  //   B5 = IR[5]; B6 = IR[6]; B7 = IR[7]; B8 = IR[8]; B9 = IR[9]; B10 = IR[10]; B11 = IR[11]; I = IR[15]
endmodule

module DR___CTRL (
  input  [15:0] IR,
  input  [3:0] T,
  output LD,
  output INR
);

  wire and_1_out, and_2_out, and_3_out, and_4_out, D0, D1, D2, D3, D4, D5, D6, D7, T0, T1, T2, T3, T4, T5,
       T6, T7, T8, T9, T10, T11, T12, T13, T14, T15;

  Decoder #(.select(3)) decoder_1 (
    .out0(D0), .out1(D1), .out2(D2), .out3(D3), .out4(D4), .out5(D5), .out6(D6), .out7(D7), .sel(IR[14:12]));  // open: en
  and and_1 (and_1_out, D0, T4);
  and and_2 (and_2_out, D1, T4);
  and and_3 (and_3_out, D2, T4);
  and and_4 (and_4_out, D6, T4);
  and and_5 (INR, D6, T5);
  Decoder #(.select(4)) decoder_2 (
    .out0(T0), .out1(T1), .out2(T2), .out3(T3), .out4(T4), .out5(T5), .out6(T6), .out7(T7), .out8(T8),
    .out9(T9), .out10(T10), .out11(T11), .out12(T12), .out13(T13), .out14(T14), .out15(T15), .sel(T));  // open: en
  or or_1 (LD, and_1_out, and_2_out, and_3_out, and_4_out);

  // Other names for the same wires on the sheet: I = IR[15]
endmodule

module IR___CTRL (
  input  R,
  input  [3:0] T,
  output LD
);

  wire T0, T1, T2, T3, T4, T5, T6, T7, T8, T9, T10, T11, T12, T13, T14, T15;

  Decoder #(.select(4)) decoder_1 (
    .out0(T0), .out1(T1), .out2(T2), .out3(T3), .out4(T4), .out5(T5), .out6(T6), .out7(T7), .out8(T8),
    .out9(T9), .out10(T10), .out11(T11), .out12(T12), .out13(T13), .out14(T14), .out15(T15), .sel(T));  // open: en
  and and_1 (LD, ~R, T1);  // AND_Gate
endmodule

module TR___CTRL (
  input  R,
  input  [3:0] T,
  output LD
);

  wire T0, T1, T2, T3, T4, T5, T6, T7, T8, T9, T10, T11, T12, T13, T14, T15;

  Decoder #(.select(4)) decoder_1 (
    .out0(T0), .out1(T1), .out2(T2), .out3(T3), .out4(T4), .out5(T5), .out6(T6), .out7(T7), .out8(T8),
    .out9(T9), .out10(T10), .out11(T11), .out12(T12), .out13(T13), .out14(T14), .out15(T15), .sel(T));  // open: en
  and and_1 (LD, R, T0);
endmodule

module OUTR___CTRL (
  input  [15:0] IR,
  input  [3:0] T,
  output LD
);

  wire D0, D1, D2, D3, D4, D5, D6, D7, T0, T1, T2, T3, T4, T5, T6, T7, T8, T9, T10, T11, T12, T13, T14, T15;

  Decoder #(.select(3)) decoder_1 (
    .out0(D0), .out1(D1), .out2(D2), .out3(D3), .out4(D4), .out5(D5), .out6(D6), .out7(D7), .sel(IR[14:12]));  // open: en
  and and_1 (LD, D7, IR[15], IR[10], T3);
  Decoder #(.select(4)) decoder_2 (
    .out0(T0), .out1(T1), .out2(T2), .out3(T3), .out4(T4), .out5(T5), .out6(T6), .out7(T7), .out8(T8),
    .out9(T9), .out10(T10), .out11(T11), .out12(T12), .out13(T13), .out14(T14), .out15(T15), .sel(T));  // open: en

  // Other names for the same wires on the sheet: B0 = IR[0]; B1 = IR[1]; B2 = IR[2]; B3 = IR[3]; B4 = IR[4];
  //   B5 = IR[5]; B6 = IR[6]; B7 = IR[7]; B8 = IR[8]; B9 = IR[9]; B10 = IR[10]; B11 = IR[11]; I = IR[15]
endmodule

module AC___CTRL (
  input  [15:0] IR,
  input  [3:0] T,
  output LD,
  output INC,
  output CLR
);

  wire and_3_out, and_4_out, and_5_out, and_6_out, and_7_out, and_8_out, and_9_out, D0, D1, D2, D3, D4, D5,
       D6, D7, p, r, T0, T1, T2, T3, T4, T5, T6, T7, T8, T9, T10, T11, T12, T13, T14, T15;

  Decoder #(.select(4)) decoder_1 (
    .out0(T0), .out1(T1), .out2(T2), .out3(T3), .out4(T4), .out5(T5), .out6(T6), .out7(T7), .out8(T8),
    .out9(T9), .out10(T10), .out11(T11), .out12(T12), .out13(T13), .out14(T14), .out15(T15), .sel(T));  // open: en
  Decoder #(.select(3)) decoder_2 (
    .out0(D0), .out1(D1), .out2(D2), .out3(D3), .out4(D4), .out5(D5), .out6(D6), .out7(D7), .sel(IR[14:12]));  // open: en
  and and_1 (p, D7, IR[15], T3);
  and and_2 (r, D7, ~IR[15], T3);  // AND_Gate
  and and_3 (and_3_out, D0, T5);
  and and_4 (and_4_out, D1, T5);
  and and_5 (and_5_out, D2, T5);
  and and_6 (and_6_out, p, IR[11]);
  and and_7 (and_7_out, r, IR[9]);
  and and_8 (and_8_out, r, IR[7]);
  and and_9 (and_9_out, r, IR[6]);
  and and_10 (INC, r, IR[5]);
  and and_11 (CLR, r, IR[11]);
  or or_1 (LD, and_3_out, and_4_out, and_5_out, and_6_out, and_7_out, and_8_out, and_9_out);

  // Other names for the same wires on the sheet: B0 = IR[0]; B1 = IR[1]; B2 = IR[2]; B3 = IR[3]; B4 = IR[4];
  //   B5 = IR[5]; B6 = IR[6]; B7 = IR[7]; B8 = IR[8]; B9 = IR[9]; B10 = IR[10]; B11 = IR[11]; I = IR[15]
endmodule

module Memory___CTRL (
  input  R,
  input  [15:0] IR,
  input  [3:0] T,
  output LD
);

  wire and_1_out, and_2_out, and_3_out, and_4_out, D0, D1, D2, D3, D4, D5, D6, D7, T0, T1, T2, T3, T4, T5,
       T6, T7, T8, T9, T10, T11, T12, T13, T14, T15;

  Decoder #(.select(3)) decoder_1 (
    .out0(D0), .out1(D1), .out2(D2), .out3(D3), .out4(D4), .out5(D5), .out6(D6), .out7(D7), .sel(IR[14:12]));  // open: en
  and and_1 (and_1_out, D5, T4);
  and and_2 (and_2_out, D3, T4);
  and and_3 (and_3_out, T1, R);
  and and_4 (and_4_out, D6, T6);
  Decoder #(.select(4)) decoder_2 (
    .out0(T0), .out1(T1), .out2(T2), .out3(T3), .out4(T4), .out5(T5), .out6(T6), .out7(T7), .out8(T8),
    .out9(T9), .out10(T10), .out11(T11), .out12(T12), .out13(T13), .out14(T14), .out15(T15), .sel(T));  // open: en
  nor nor_1 (LD, and_1_out, and_2_out, and_3_out, and_4_out);

  // Other names for the same wires on the sheet: I = IR[15]
endmodule

module AR___CTRl (
  input  R,
  input  [15:0] IR,
  input  [3:0] T,
  output LD,
  output INR,
  output CLR
);

  wire and_1_out, and_2_out, and_3_out, D0, D1, D2, D3, D4, D5, D6, D7, T0, T1, T2, T3, T4, T5, T6, T7, T8,
       T9, T10, T11, T12, T13, T14, T15;

  Decoder #(.select(3)) decoder_1 (
    .out0(D0), .out1(D1), .out2(D2), .out3(D3), .out4(D4), .out5(D5), .out6(D6), .out7(D7), .sel(IR[14:12]));  // open: en
  Decoder #(.select(4)) decoder_2 (
    .out0(T0), .out1(T1), .out2(T2), .out3(T3), .out4(T4), .out5(T5), .out6(T6), .out7(T7), .out8(T8),
    .out9(T9), .out10(T10), .out11(T11), .out12(T12), .out13(T13), .out14(T14), .out15(T15), .sel(T));  // open: en
  and and_1 (and_1_out, ~D7, IR[15], T3);  // AND_Gate
  and and_2 (and_2_out, T2, ~R);  // AND_Gate
  and and_3 (and_3_out, ~R, T0);  // AND_Gate
  and and_4 (INR, D5, T4);
  and and_5 (CLR, T0, R);
  or or_1 (LD, and_1_out, and_2_out, and_3_out);

  // Other names for the same wires on the sheet: I = IR[15]
endmodule

module ALU___CTRL (
  input  [15:0] IR,
  input  [3:0] T,
  output [2:0] out_3
);

  wire ADD, AND, COM, D0, D1, D2, D3, D4, D5, D6, D7, DR, INPR, LD, p, r, SHL, SHR, T0, T1, T2, T3, T4, T5,
       T6, T7, T8, T9, T10, T11, T12, T13, T14, T15;

  Decoder #(.select(4)) decoder_1 (
    .out0(T0), .out1(T1), .out2(T2), .out3(T3), .out4(T4), .out5(T5), .out6(T6), .out7(T7), .out8(T8),
    .out9(T9), .out10(T10), .out11(T11), .out12(T12), .out13(T13), .out14(T14), .out15(T15), .sel(T));  // open: en
  Decoder #(.select(3)) decoder_2 (
    .out0(D0), .out1(D1), .out2(D2), .out3(D3), .out4(D4), .out5(D5), .out6(D6), .out7(D7), .sel(IR[14:12]));  // open: en
  and and_1 (r, D7, ~IR[15], T3);  // AND_Gate
  and and_2 (p, D7, IR[15], T3);
  and and_3 (AND, D0, T5);
  and and_4 (ADD, D1, T5);
  and and_5 (DR, D2, T5);
  and and_6 (INPR, p, IR[11]);
  and and_7 (COM, r, IR[9]);
  and and_8 (SHR, r, IR[7]);
  and and_9 (SHL, r, IR[6]);
  Priority_Encoder priority_encoder_1 (
    .in0(LD), .in1(AND), .in2(ADD), .in3(COM), .in4(DR), .in5(INPR), .in6(SHR), .in7(SHL), .out(out_3));  // open: en_in, gs, en_out
  nor nor_1 (LD, AND, ADD, COM, DR, INPR, SHR, SHL);

  // Other names for the same wires on the sheet: B0 = IR[0]; B1 = IR[1]; B2 = IR[2]; B3 = IR[3]; B4 = IR[4];
  //   B5 = IR[5]; B6 = IR[6]; B7 = IR[7]; B8 = IR[8]; B9 = IR[9]; B10 = IR[10]; B11 = IR[11]; I = IR[15]
endmodule

module E___CTRL (
  input  [15:0] IR,
  input  [3:0] T,
  output CLR,
  output CMP,
  output LD
);

  wire and_5_out, and_6_out, and_7_out, D0, D1, D2, D3, D4, D5, D6, D7, p, r, T0, T1, T2, T3, T4, T5, T6, T7,
       T8, T9, T10, T11, T12, T13, T14, T15;

  Decoder #(.select(4)) decoder_1 (
    .out0(T0), .out1(T1), .out2(T2), .out3(T3), .out4(T4), .out5(T5), .out6(T6), .out7(T7), .out8(T8),
    .out9(T9), .out10(T10), .out11(T11), .out12(T12), .out13(T13), .out14(T14), .out15(T15), .sel(T));  // open: en
  Decoder #(.select(3)) decoder_2 (
    .out0(D0), .out1(D1), .out2(D2), .out3(D3), .out4(D4), .out5(D5), .out6(D6), .out7(D7), .sel(IR[14:12]));  // open: en
  and and_1 (p, D7, IR[15], T3);
  and and_2 (r, D7, ~IR[15], T3);  // AND_Gate
  and and_3 (CLR, r, IR[10]);
  and and_4 (CMP, r, IR[8]);
  and and_5 (and_5_out, r, IR[7]);
  and and_6 (and_6_out, r, IR[6]);
  or or_1 (LD, and_5_out, and_6_out, and_7_out);
  and and_7 (and_7_out, T5, D1);

  // Other names for the same wires on the sheet: B0 = IR[0]; B1 = IR[1]; B2 = IR[2]; B3 = IR[3]; B4 = IR[4];
  //   B5 = IR[5]; B6 = IR[6]; B7 = IR[7]; B8 = IR[8]; B9 = IR[9]; B10 = IR[10]; B11 = IR[11]; I = IR[15]
endmodule

module T___CTRL (
  input  R,
  input  [15:0] IR,
  input  [3:0] T,
  output out_4
);

  wire and_1_out, and_2_out, and_3_out, and_4_out, and_5_out, and_6_out, and_7_out, and_8_out, and_9_out,
       and_10_out, D0, D1, D2, D3, D4, D5, D6, D7, T0, T1, T2, T3, T4, T5, T6, T7, T8, T9, T10, T11, T12,
       T13, T14, T15;

  Decoder #(.select(4)) decoder_1 (
    .out0(T0), .out1(T1), .out2(T2), .out3(T3), .out4(T4), .out5(T5), .out6(T6), .out7(T7), .out8(T8),
    .out9(T9), .out10(T10), .out11(T11), .out12(T12), .out13(T13), .out14(T14), .out15(T15), .sel(T));  // open: en
  Decoder #(.select(3)) decoder_2 (
    .out0(D0), .out1(D1), .out2(D2), .out3(D3), .out4(D4), .out5(D5), .out6(D6), .out7(D7), .sel(IR[14:12]));  // open: en
  and and_1 (and_1_out, R, T3);
  and and_2 (and_2_out, D0, T6);
  and and_3 (and_3_out, D1, T6);
  and and_4 (and_4_out, D2, T6);
  and and_5 (and_5_out, D5, T6);
  and and_6 (and_6_out, D3, T5);
  and and_7 (and_7_out, D4, T5);
  and and_8 (and_8_out, D6, T7);
  and and_9 (and_9_out, D7, ~IR[15], T4);  // AND_Gate
  and and_10 (and_10_out, D7, IR[15], T4);
  or or_1 (out_4, and_1_out, and_2_out, and_3_out, and_4_out, and_5_out, and_6_out, and_7_out, and_8_out, and_9_out, and_10_out);

  // Other names for the same wires on the sheet: B0 = IR[0]; B1 = IR[1]; B2 = IR[2]; B3 = IR[3]; B4 = IR[4];
  //   B5 = IR[5]; B6 = IR[6]; B7 = IR[7]; B8 = IR[8]; B9 = IR[9]; B10 = IR[10]; B11 = IR[11]; I = IR[15]
endmodule

module BUS (
  input  [11:0] PC,
  input  [15:0] TR,
  input  [15:0] M,
  input  [15:0] IR,
  input  [11:0] AR,
  input  [15:0] DR,
  input  [15:0] AC,
  input  [2:0] in_8,
  output [15:0] out_9
);

  Multiplexer #(.select(3), .width(16)) multiplexer_1 (
    .in1(M), .in2({4'b0000, AR}), .in3({4'b0000, PC}), .in4(DR), .in5(AC), .in6(IR), .in7(TR), .out(out_9),
    .sel(in_8));  // open: in0, en
endmodule
